// Logisim project harward_arc terminal.circ as structural Verilog: 10 circuits, main circuit 8 bit to 7 (-high)
module main (
);

  wire addr_fe_bit_7, and_1_out, and_2_out, and_3_out, and_4_out, and_5_out, button_1_out, button_2_out,
       cdm_8_mark5_1_data_inst, Cl, code, comparator_1_eq, comparator_2_eq, comparator_3_eq, comparator_4_eq,
       data, end_message, keyboard_1_avail, keyboard_2_clean, keyboard_2_increment_rundom_index,
       keyboard_2_keyboard_clock, keyboard_2_turn_off_on, keyboard_2_update_random_number_for_bot,
       keyboard_2_update_random_number_for_field, load_cell_1_out, load_cell_2_out, load_cell_3_out, mem,
       message_box_1_terminal_clean, message_box_1_terminal_clock, not_1_out, or_1_out, or_2_out, rd_wr,
       store_cell_1_p7, write_field_1_dicplay_clean, write_field_1_display_clock,
       write_field_2_dicplay_clean, write_field_2_display_clock;
  wire [1:0] undriven_3;
  wire [3:0] number_of_living_cells_1_high, number_of_living_cells_1_low, number_of_living_cells_2_high,
       number_of_living_cells_2_low;
  wire [6:0] ascii_cod, message_box_1_ascii_code_out, write_field_1_ascii_code, write_field_2_ascii_code;
  wire [7:0] addr, addr_8_15, bot_s_cell, cdm_8_mark5_1_data_out, cdm_8_mark5_1_ps, cdm_8_mark5_1_r0,
       cdm_8_mark5_1_r1, cdm_8_mark5_1_r2, cdm_8_mark5_1_r3, cdm_8_mark5_1_sp, controlled_buffer_2_out,
       controlled_buffer_5_out, data_8_bit, keyboard_bits_in, keyboard_bits_out, random_number, register_2_q,
       register_3_q, undriven, undriven_2;
  wire [15:0] cdm_8_mark5_1_pc;
  wire [19:0] display_ship_1_out_2, display_ship_1_out_3, display_ship_1_out_4, display_ship_1_out_5,
       display_ship_1_out_6, display_ship_1_out_7, display_ship_1_out_8, display_ship_1_out_9,
       display_ship_1_out_10, display_ship_1_out_11, display_ship_1_out_12, display_ship_1_out_13,
       display_ship_1_out_14, display_ship_1_out_15, display_ship_1_out_16, display_ship_1_out_17,
       display_ship_1_out_18, display_ship_1_out_19, display_ship_1_out_20, display_ship_1_out_21,
       display_ship_1_out_22, display_ship_1_out_23, display_ship_1_out_24, display_ship_1_out_25,
       display_ship_1_out_26, display_ship_1_out_27, display_ship_1_out_28, display_ship_1_out_29,
       display_ship_1_out_30, display_ship_1_out_31, display_ship_1_out_32, display_ship_1_out_33;

  // Probe on cdm_8_mark5_1_r0
  // Probe on cdm_8_mark5_1_r2
  // Probe on cdm_8_mark5_1_r3
  // Probe on cdm_8_mark5_1_r1
  Clock clock_1 (.out(Cl));
  // Probe on cdm_8_mark5_1_sp
  // Probe on cdm_8_mark5_1_pc
  // Probe on cdm_8_mark5_1_ps
  CdM_8_mark5 cdm_8_mark5_1 (
    .clock(Cl), .addr({addr_8_15, addr}), .mem_read(rd_wr), .mem_cycle(mem),
    .data_inst(cdm_8_mark5_1_data_inst), .data_out(cdm_8_mark5_1_data_out),
    .data_in(controlled_buffer_2_out), .r0(cdm_8_mark5_1_r0), .r1(cdm_8_mark5_1_r1), .r2(cdm_8_mark5_1_r2),
    .r3(cdm_8_mark5_1_r3), .PC(cdm_8_mark5_1_pc), .SP(cdm_8_mark5_1_sp), .PS(cdm_8_mark5_1_ps));  // open: IAck, IRQ, vec, halted
  Comparator comparator_1 (.a(addr_8_15), .b({8{1'b0}}), .eq(comparator_1_eq));  // open: gt, lt
  Comparator comparator_2 (.a(8'hfe), .b(addr), .eq(comparator_2_eq));  // open: gt, lt
  // Probe on cdm_8_mark5_1_data_out
  and and_1 (and_1_out, comparator_1_eq, data, comparator_2_eq);
  Comparator comparator_3 (.a(8'h7), .b(addr), .eq(comparator_3_eq));  // open: gt, lt
  assign data_8_bit = not_1_out ? cdm_8_mark5_1_data_out : 8'bz;  // Controlled_Buffer controlled_buffer_1
  not not_1 (not_1_out, rd_wr);
  assign controlled_buffer_2_out = rd_wr ? data_8_bit : 8'bz;  // Controlled_Buffer controlled_buffer_2
  and and_2 (and_2_out, ~rd_wr, data, comparator_3_eq);  // AND_Gate
  Decoder #(.disabled(0)) decoder_1 (.out0(code), .out1(data), .sel(cdm_8_mark5_1_data_inst), .en(mem));
  Register register_1 (.D(data_8_bit), .en(and_1_out), .Q(keyboard_bits_in), .clk(Cl));  // open: clr
  Register register_2 (.D(undriven), .en(and_2_out), .Q(register_2_q), .clk(Cl));  // open: clr
  Comparator comparator_4 (.a(8'h8), .b(addr), .eq(comparator_4_eq));  // open: gt, lt
  // Probe on {addr_8_15, addr}
  load_cell load_cell_1 (.rd_wr(rd_wr), .data(data), .\const (8'hf8), .addr(addr), .out(load_cell_1_out));
  and and_3 (and_3_out, rd_wr, data, comparator_4_eq);
  assign data_8_bit = and_4_out ? keyboard_bits_out : 8'bz;  // Controlled_Buffer controlled_buffer_3
  and and_4 (and_4_out, rd_wr, data, comparator_2_eq);
  assign data_8_bit = load_cell_1_out ? random_number : 8'bz;  // Controlled_Buffer controlled_buffer_4
  assign controlled_buffer_5_out = and_3_out ? register_3_q : 8'bz;  // Controlled_Buffer controlled_buffer_5
  Register register_3 (.D(undriven_2), .en(and_3_out), .Q(register_3_q), .clk(Cl));  // open: clr
  load_cell load_cell_2 (.rd_wr(rd_wr), .data(data), .\const (8'hfb), .addr(addr), .out(load_cell_2_out));
  and and_5 (and_5_out, ~or_1_out, data);  // AND_Gate
  or or_1 (or_1_out, and_4_out, load_cell_1_out, load_cell_2_out, load_cell_3_out);
  assign data_8_bit = load_cell_2_out ? bot_s_cell : 8'bz;  // Controlled_Buffer controlled_buffer_6
  write_field write_field_1 (
    .rd_wr(rd_wr), .data_1_bit(data), .bot_user_adress(8'hfc), .addr(addr), .data_8_bit(data_8_bit),
    .ASCII_code(write_field_1_ascii_code), .display_clock(write_field_1_display_clock),
    .dicplay_clean(write_field_1_dicplay_clean));
  TTY #(.rows(12), .cols(13)) tty_1 (
    .data(write_field_1_ascii_code), .clk(write_field_1_display_clock), .clr(write_field_1_dicplay_clean));  // open: we
  // RAM ram_1: pin names not known; wires that end beside it: {addr_8_15, addr}, code, 1'b1, data_8_bit
  // RAM ram_2: pin names not known; wires that end beside it: addr, and_5_out, Cl, rd_wr, data_8_bit
  load_cell load_cell_3 (.rd_wr(rd_wr), .data(data), .\const (8'hfd), .addr(addr), .out(load_cell_3_out));
  Hex_Digit_Display hex_digit_display_1 (.value(number_of_living_cells_1_high));  // open: dp
  Hex_Digit_Display hex_digit_display_2 (.value(number_of_living_cells_1_low));  // open: dp
  number_of_living_cells number_of_living_cells_1 (
    .data_8_bit(data_8_bit), .rd_wr(rd_wr), .data_1_bit(data), .Cl(Cl), .\const (8'hf0), .addr(addr),
    .low(number_of_living_cells_1_low), .high(number_of_living_cells_1_high));
  assign data_8_bit = load_cell_3_out ? {1'b0, ascii_cod} : 8'bz;  // Controlled_Buffer controlled_buffer_7
  // Probe on {1'b0, ascii_cod}
  message_box message_box_1 (
    .clock(Cl), .data_8_bit(data_8_bit), .rd_wr(rd_wr), .data_1_bit(data), .addr(addr),
    .ASCII_code_out(message_box_1_ascii_code_out), .terminal_clock(message_box_1_terminal_clock),
    .terminal_clean(message_box_1_terminal_clean), .end_message(end_message),
    .addr_fe__bit___7(addr_fe_bit_7), .buttom(button_1_out));
  TTY #(.cols(50)) tty_2 (
    .data(message_box_1_ascii_code_out), .clk(message_box_1_terminal_clock),
    .clr(message_box_1_terminal_clean));  // open: we
  Button button_1 (.out(button_1_out));
  display_ship display_ship_1 (
    .out_2(display_ship_1_out_2), .out_3(display_ship_1_out_3), .out_4(display_ship_1_out_4),
    .out_5(display_ship_1_out_5), .out_6(display_ship_1_out_6), .out_7(display_ship_1_out_7),
    .out_8(display_ship_1_out_8), .out_9(display_ship_1_out_9), .out_10(display_ship_1_out_10),
    .out_11(display_ship_1_out_11), .out_12(display_ship_1_out_12), .out_13(display_ship_1_out_13),
    .out_14(display_ship_1_out_14), .out_15(display_ship_1_out_15), .out_16(display_ship_1_out_16),
    .out_17(display_ship_1_out_17), .out_18(display_ship_1_out_18), .out_19(display_ship_1_out_19),
    .out_20(display_ship_1_out_20), .out_21(display_ship_1_out_21), .out_22(display_ship_1_out_22),
    .out_23(display_ship_1_out_23), .out_24(display_ship_1_out_24), .out_25(display_ship_1_out_25),
    .out_26(display_ship_1_out_26), .out_27(display_ship_1_out_27), .out_28(display_ship_1_out_28),
    .out_29(display_ship_1_out_29), .out_30(display_ship_1_out_30), .out_31(display_ship_1_out_31),
    .out_32(display_ship_1_out_32), .out_33(display_ship_1_out_33), .num_picture(undriven_3));
  DotMatrix #(.matrixcols(32), .matrixrows(20)) dotmatrix_1 (
    .col0(display_ship_1_out_2), .col1(display_ship_1_out_3), .col2(display_ship_1_out_4),
    .col3(display_ship_1_out_5), .col4(display_ship_1_out_6), .col5(display_ship_1_out_7),
    .col6(display_ship_1_out_8), .col7(display_ship_1_out_9), .col8(display_ship_1_out_10),
    .col9(display_ship_1_out_11), .col10(display_ship_1_out_12), .col11(display_ship_1_out_13),
    .col12(display_ship_1_out_14), .col13(display_ship_1_out_15), .col14(display_ship_1_out_16),
    .col15(display_ship_1_out_17), .col16(display_ship_1_out_18), .col17(display_ship_1_out_19),
    .col18(display_ship_1_out_20), .col19(display_ship_1_out_21), .col20(display_ship_1_out_22),
    .col21(display_ship_1_out_23), .col22(display_ship_1_out_24), .col23(display_ship_1_out_25),
    .col24(display_ship_1_out_26), .col25(display_ship_1_out_27), .col26(display_ship_1_out_28),
    .col27(display_ship_1_out_29), .col28(display_ship_1_out_30), .col29(display_ship_1_out_31),
    .col30(display_ship_1_out_32), .col31(display_ship_1_out_33));
  Keyboard #(.buflen(2)) keyboard_1 (
    .clk(keyboard_2_keyboard_clock), .re(keyboard_2_turn_off_on), .clr(or_2_out), .avail(keyboard_1_avail),
    .data(ascii_cod));
  or or_2 (or_2_out, keyboard_2_clean, button_2_out);
  Button button_2 (.out(button_2_out));
  random_field random_field_1 (
    .cl(Cl), .cell_data(bot_s_cell), .update_register(keyboard_2_update_random_number_for_field),
    .update_counter(keyboard_2_increment_rundom_index));
  random_number random_number_1 (
    .cl(Cl), .cell_data(random_number),
    .update_random_number_for_field(keyboard_2_update_random_number_for_bot));
  keyboard keyboard_2 (
    .empty_keyboard(keyboard_1_avail), .keyboard_bits_in(keyboard_bits_in), .end_message(end_message),
    .addr_fe_bit_7(addr_fe_bit_7), .keyboard_bits_out(keyboard_bits_out),
    .keyboard_clock(keyboard_2_keyboard_clock), .turn_off_on(keyboard_2_turn_off_on),
    .clean(keyboard_2_clean), .update_random_number_for_field(keyboard_2_update_random_number_for_field),
    .increment_rundom_index(keyboard_2_increment_rundom_index),
    .update_random_number_for_bot(keyboard_2_update_random_number_for_bot));
  write_field write_field_2 (
    .rd_wr(rd_wr), .data_1_bit(data), .bot_user_adress(8'hfa), .addr(addr), .data_8_bit(data_8_bit),
    .ASCII_code(write_field_2_ascii_code), .display_clock(write_field_2_display_clock),
    .dicplay_clean(write_field_2_dicplay_clean));
  TTY #(.rows(12), .cols(13)) tty_3 (
    .data(write_field_2_ascii_code), .clk(write_field_2_display_clock), .clr(write_field_2_dicplay_clean));  // open: we
  // store_cell store_cell_1: pin names not known; wires that end beside it: rd_wr, data_8_bit, data, 8'hf9, addr, Cl, store_cell_1_p7, store_cell_1_p7
  Hex_Digit_Display hex_digit_display_3 (.value(number_of_living_cells_2_low));  // open: dp
  Hex_Digit_Display hex_digit_display_4 (.value(number_of_living_cells_2_high));  // open: dp
  number_of_living_cells number_of_living_cells_2 (
    .data_8_bit(data_8_bit), .rd_wr(rd_wr), .data_1_bit(data), .Cl(Cl), .\const (8'hf1), .addr(addr),
    .low(number_of_living_cells_2_low), .high(number_of_living_cells_2_high));

  // Notes on the sheet:
  //   Терминал вывода поля пользователя
  //   Red Button
  //   терминал общения с пользователем
  //   clean button
  //   Терминал вывода поля бота
endmodule

module _8_bit_to_7___high (
  input  [7:0] entrance,
  output [6:0] bus_0
);


  assign bus_0 = entrance[6:0];
endmodule

module message_box (
  input  clock,
  input  [7:0] data_8_bit,
  input  rd_wr,
  input  data_1_bit,
  input  [7:0] addr,
  input  buttom,
  input  addr_fe__bit___7,
  output [6:0] ASCII_code_out,
  output terminal_clock,
  output terminal_clean,
  output end_message
);

  wire and_1_out, and_3_out, and_5_out, cmp, comparator_1_eq, counter_1_carry, not_1_out, or_1_out, or_2_out,
       or_3_out, register_1_q, register_2_q;
  wire [3:0] counter_1_q;
  wire [7:0] counter_2_q, demultiplexer_1_out1, rom_1_data;

  and and_1 (and_1_out, data_1_bit, ~rd_wr);  // AND_Gate
  Demultiplexer #(.width(8), .enable("false")) demultiplexer_1 (
    .out1(demultiplexer_1_out1), .in(addr), .sel(and_1_out));  // open: out0
  Comparator comparator_1 (.a({8{1'b1}}), .b(demultiplexer_1_out1), .eq(comparator_1_eq));  // open: gt, lt
  and and_2 (terminal_clean, ~rd_wr, data_1_bit, comparator_1_eq);  // AND_Gate
  not not_1 (not_1_out, terminal_clean);
  and and_3 (and_3_out, terminal_clean, clock);
  Counter #(.width(4), .max('hf), .trigger("falling")) counter_1 (
    .Q(counter_1_q), .carry(counter_1_carry), .clk(terminal_clock), .clr(terminal_clean));  // open: load, D, count
  Counter #(.trigger("falling")) counter_2 (
    .load(terminal_clean), .D(data_8_bit), .count(not_1_out), .Q(counter_2_q), .clk(or_1_out));  // open: carry, clr
  or or_1 (or_1_out, and_3_out, counter_1_carry);
  or or_2 (or_2_out, register_1_q, cmp);
  Register #(.width(1)) register_1 (.D(or_2_out), .Q(register_1_q), .clk(clock), .clr(terminal_clean));  // open: en
  ROM #(.addrWidth(12)) rom_1 (.addr({counter_2_q, counter_1_q}), .data(rom_1_data), .sel(1'b1));
  and and_4 (terminal_clock, ~register_1_q, clock);  // AND_Gate
  _8_bit_to_7___high u_8_bit_to_7_high_1 (.entrance(rom_1_data), .bus_0(ASCII_code_out));
  Comparator #(.width(7)) comparator_2 (.a(ASCII_code_out), .b({7{1'b0}}), .eq(cmp));  // open: gt, lt
  or or_3 (or_3_out, register_2_q, buttom);
  and and_5 (and_5_out, or_3_out, ~addr_fe__bit___7);  // AND_Gate
  Register #(.width(1)) register_2 (.D(and_5_out), .Q(register_2_q), .clk(clock));  // open: en, clr
  and and_6 (end_message, cmp, register_2_q);

  // Other names for the same wires on the sheet: Cl = clock; cl_input = terminal_clock; cmp_res = terminal_clean

  // Notes on the sheet:
  //   эта часть для загрузки адреса
  //   ___
  //   >
  //   ^
  //   |
  //   Эта часть для увеличения счётчика адреса
  //   4 младших за само сообщение
  //   8 старших за номер сообщения
  //   contents of rom_1 (hex, n*v repeats v):
  //   54 68 69 73 20 67 61 6d 65 20 69 73 20 22 53 65 61 20 42 61 74 74 6c 65 22 21 a 48 61 76 65 20 61 20
  //   67 6f 6f 64 20 74 69 6d 65 21 6*a 43 6c 69 63 6b 20 74 68 65 20 22 52 65 64 20 42 75 74 74 6f 6e 22
  //   20 74 6f 20 63 6f 6e 74 69 6e 75 65 2e 11*0 57 65 6c 6c 2c 20 77 65 20 6e 65 65 64 20 74 6f 20 61 72
  //   72 61 6e 67 65 20 74 68 65 20 73 68 69 70 73 2e a 54 68 65 72 65 20 69 73 20 61 20 6b 65 79 62 6f 61
  //   72 64 20 62 65 6c 6f 77 2e a 45 6e 74 65 72 20 74 68 65 20 63 6f 6f 72 64 69 6e 61 74 65 73 20 6f 66
  //   20 74 68 65 20 73 68 69 70 73 a 49 20 77 69 6c 6c 20 61 73 6b 20 66 6f 72 2e a 46 69 72 73 74 20 61
  //   20 6c 65 74 74 65 72 2c 20 74 68 65 6e 20 61 20 64 69 67 69 74 2e a 46 6f 72 20 65 78 61 6d 70 6c 65
  //   3a 20 41 32 20 6f 72 20 61 32 a a 43 6c 69 63 6b 20 74 68 65 20 22 52 65 64 20 42 75 74 74 6f 6e 22
  //   20 74 6f 20 63 6f 6e 74 69 6e 75 65 2e 6*0 53 68 69 70 73 20 63 61 6e 6e 6f 74 20 62 65 20 6e 65 69
  //   67 68 62 6f 72 73 2e a 59 6f 75 20 77 69 6c 6c 20 68 61 76 65 3a a 31 20 73 68 69 70 20 77 69 74 68
  //   20 61 20 6c 65 6e 67 74 68 20 6f 66 20 34 2e a 32 20 73 68 69 70 73 20 33 20 69 6e 20 6c 65 6e 67 74
  //   68 2e a 33 20 73 68 69 70 73 20 32 20 69 6e 20 6c 65 6e 67 74 68 2e a 34 20 73 68 69 70 73 20 31 20
  //   69 6e 20 6c 65 6e 67 74 68 2e a a 43 6c 69 63 6b 20 74 68 65 20 22 52 65 64 20 42 75 74 74 6f 6e 22
  //   20 74 6f 20 63 6f 6e 74 69 6e 75 65 2e 8*0 45 6e 74 65 72 20 74 68 65 20 66 69 72 73 74 20 63 6f 6f
  //   72 64 69 6e 61 74 65 a 6f 66 20 74 68 65 20 73 68 69 70 20 6f 66 20 6c 65 6e 67 74 68 20 34 6*a 43
  //   6c 69 63 6b 20 74 68 65 20 22 52 65 64 20 42 75 74 74 6f 6e 22 20 74 6f 20 63 6f 6e 74 69 6e 75 65
  //   2e 5*0 45 6e 74 65 72 20 74 68 65 20 73 65 63 6f 6e 64 20 63 6f 6f 72 64 69 6e 61 74 65 a 6f 66 20
  //   74 68 65 20 73 68 69 70 20 6f 66 20 6c 65 6e 67 74 68 20 34 6*a 43 6c 69 63 6b 20 74 68 65 20 22 52
  //   65 64 20 42 75 74 74 6f 6e 22 20 74 6f 20 63 6f 6e 74 69 6e 75 65 2e 4*0 45 6e 74 65 72 20 74 68 65
  //   20 66 69 72 73 74 20 63 6f 6f 72 64 69 6e 61 74 65 a 6f 66 20 74 68 65 20 73 68 69 70 20 6f 66 20 6c
  //   65 6e 67 74 68 20 33 6*a 43 6c 69 63 6b 20 74 68 65 20 22 52 65 64 20 42 75 74 74 6f 6e 22 20 74 6f
  //   20 63 6f 6e 74 69 6e 75 65 2e 5*0 45 6e 74 65 72 20 74 68 65 20 73 65 63 6f 6e 64 20 63 6f 6f 72 64
  //   69 6e 61 74 65 a 6f 66 20 74 68 65 20 73 68 69 70 20 6f 66 20 6c 65 6e 67 74 68 20 33 6*a 43 6c 69
  //   63 6b 20 74 68 65 20 22 52 65 64 20 42 75 74 74 6f 6e 22 20 74 6f 20 63 6f 6e 74 69 6e 75 65 2e 4*0
  //   45 6e 74 65 72 20 74 68 65 20 66 69 72 73 74 20 63 6f 6f 72 64 69 6e 61 74 65 a 6f 66 20 74 68 65 20
  //   73 68 69 70 20 6f 66 20 6c 65 6e 67 74 68 20 32 6*a 43 6c 69 63 6b 20 74 68 65 20 22 52 65 64 20 42
  //   75 74 74 6f 6e 22 20 74 6f 20 63 6f 6e 74 69 6e 75 65 2e 5*0 45 6e 74 65 72 20 74 68 65 20 73 65 63
  //   6f 6e 64 20 63 6f 6f 72 64 69 6e 61 74 65 a 6f 66 20 74 68 65 20 73 68 69 70 20 6f 66 20 6c 65 6e 67
  //   74 68 20 32 6*a 43 6c 69 63 6b 20 74 68 65 20 22 52 65 64 20 42 75 74 74 6f 6e 22 20 74 6f 20 63 6f
  //   6e 74 69 6e 75 65 2e 4*0 45 6e 74 65 72 20 6f 6e 65 20 63 6f 6f 72 64 69 6e 61 74 65 20 66 6f 72 20
  //   61 20 73 68 69 70 20 6f 66 20 6c 65 6e 67 74 68 20 31 6*a 43 6c 69 63 6b 20 74 68 65 20 22 52 65 64
  //   20 42 75 74 74 6f 6e 22 20 74 6f 20 63 6f 6e 74 69 6e 75 65 2e 12*0 54 68 65 20 66 69 65 6c 64 20 69
  //   73 20 62 65 69 6e 67 20 70 72 69 6e 74 65 64 2e a 50 6c 65 61 73 65 20 77 61 69 74 21 a 20 20 20 50
  //   6c 65 61 73 65 20 77 61 69 74 21 a 6*20 50 6c 65 61 73 65 20 77 61 69 74 21 a 9*20 50 6c 65 61 73 65
  //   20 77 61 69 74 21 a 12*20 50 6c 65 61 73 65 20 77 61 69 74 21 a 15*20 50 6c 65 61 73 65 20 77 61 69
  //   74 21 a 18*20 50 6c 65 61 73 65 20 77 61 69 74 21 11*0 59 6f 75 20 68 61 76 65 20 65 6e 74 65 72 65
  //   64 20 61 6e 20 69 6e 63 6f 72 72 65 63 74 20 73 79 6d 62 6f 6c 73 2e a 50 6c 65 61 73 65 20 74 72 79
  //   20 61 67 61 69 6e 2e 6*a 43 6c 69 63 6b 20 74 68 65 20 22 52 65 64 20 42 75 74 74 6f 6e 22 20 74 6f
  //   20 63 6f 6e 74 69 6e 75 65 2e 15*0 59 6f 75 20 68 61 76 65 20 65 6e 74 65 72 65 64 20 63 6f 6f 72 64
  //   69 6e 61 74 65 73 a 6f 66 20 69 6e 63 6f 72 72 65 63 74 20 6c 65 6e 67 74 68 2e a 50 6c 65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
endmodule

module write_field (
  input  rd_wr,
  input  data_1_bit,
  input  [7:0] bot_user_adress,
  input  [7:0] addr,
  input  [7:0] data_8_bit,
  output display_clock,
  output dicplay_clean,
  output [6:0] ASCII_code
);

  wire and_1_out, and_2_out, and_3_out, comparator_1_eq, comparator_2_eq;
  wire [7:0] demultiplexer_1_out1;

  Demultiplexer #(.width(8), .enable("false")) demultiplexer_1 (
    .out1(demultiplexer_1_out1), .in(addr), .sel(and_1_out));  // open: out0
  Comparator comparator_1 (.a(bot_user_adress), .b(demultiplexer_1_out1), .eq(comparator_1_eq));  // open: gt, lt
  and and_1 (and_1_out, data_1_bit, ~rd_wr);  // AND_Gate
  and and_2 (and_2_out, ~rd_wr, data_1_bit, and_3_out);  // AND_Gate
  and and_3 (and_3_out, and_1_out, comparator_1_eq);
  and and_4 (display_clock, 1'b1, and_2_out);
  // Probe on data_8_bit
  Multiplexer #(.select(5), .width(7), .enable("false")) multiplexer_1 (
    .in0(7'b1111110), .in1(7'b0100011), .in2(7'b0100001), .in3(7'b1011000), .in4(7'b1101111),
    .in5(7'b0100000), .in6(7'b0110000), .in7(7'b0110001), .in8(7'b0110010), .in9(7'b0110011),
    .in10(7'b0110100), .in11(7'b0110101), .in12(7'b0110110), .in13(7'b0110111), .in14(7'b0111000),
    .in15(7'b0111001), .in16(7'b1000001), .in17(7'b1000010), .in18(7'b1000011), .in19(7'b1000100),
    .in20(7'b1000101), .in21(7'b1000110), .in22(7'b1000111), .in23(7'b1001000), .in24(7'b1001001),
    .in25(7'b1001010), .in26(7'b0001101), .in27(7'b0100011), .in28(7'b0100000), .in29(7'b0100000),
    .in30(7'b0100000), .in31({7{1'b0}}), .out(ASCII_code), .sel(data_8_bit[4:0]));
  Comparator comparator_2 (.a(8'h1f), .b(data_8_bit), .eq(comparator_2_eq));  // open: gt, lt
  and and_5 (dicplay_clean, display_clock, comparator_2_eq);
  TTY #(.rows(12), .cols(13)) tty_1 (.data(ASCII_code), .clk(display_clock), .clr(dicplay_clean));  // open: we
  // Probe on ASCII_code

  // Notes on the sheet:
  //   для очистки дисплея 31
  //   0 - ничего (~)
  //   1 - корабль (#)
  //   2 - занято (!)
  //   5 - пробел
  //   27 - корабль, но на поле бота (~)
  //   3 - подбитый корабль (X)
  //   4 - выстрел в ничего (* или +)
  //   6 - 15 = figures
  //   16 - 25 = letters
  //   26 - '\n' (Enter)
endmodule

module number_of_living_cells (
  input  [7:0] data_8_bit,
  input  rd_wr,
  input  data_1_bit,
  input  Cl,
  input  [7:0] \const ,
  input  [7:0] addr,
  output [3:0] high,
  output [3:0] low
);

  wire and_1_out, comparator_1_eq;
  wire [7:0] register_1_q;
  wire [7:4] divider_1_out, divider_1_rem;

  Comparator comparator_1 (.a(\const ), .b(addr), .eq(comparator_1_eq));  // open: gt, lt
  and and_1 (and_1_out, ~rd_wr, data_1_bit, comparator_1_eq);  // AND_Gate
  Register register_1 (.D(data_8_bit), .en(and_1_out), .Q(register_1_q), .clk(Cl));  // open: clr
  Divider divider_1 (
    .a(register_1_q), .b(8'ha), .out({divider_1_out, high}), .rem({divider_1_rem, low}));  // open: upper
endmodule

module store_cell (
  input  rd_wr,
  input  [7:0] data_8_bit,
  input  data_1_bit,
  input  [7:0] \const ,
  input  cl,
  input  [7:0] addr,
  output [7:0] \output 
);

  wire and_1_out, comparator_1_eq;

  Comparator comparator_1 (.a(\const ), .b(addr), .eq(comparator_1_eq));  // open: gt, lt
  and and_1 (and_1_out, ~rd_wr, data_1_bit, comparator_1_eq);  // AND_Gate
  Register register_1 (.D(data_8_bit), .en(and_1_out), .Q(\output ), .clk(cl));  // open: clr
endmodule

module load_cell (
  input  rd_wr,
  input  data,
  input  [7:0] \const ,
  input  [7:0] addr,
  output out
);

  wire comparator_1_eq;

  Comparator comparator_1 (.a(\const ), .b(addr), .eq(comparator_1_eq));  // open: gt, lt
  and and_1 (out, rd_wr, data, comparator_1_eq);
endmodule

module keyboard (
  input  empty_keyboard,
  input  [7:0] keyboard_bits_in,
  input  end_message,
  output keyboard_clock,
  output turn_off_on,
  output clean,
  output [7:0] keyboard_bits_out,
  output addr_fe_bit_7,
  output update_random_number_for_field,
  output increment_rundom_index,
  output update_random_number_for_bot
);


  assign addr_fe_bit_7 = keyboard_bits_in[7];
  assign clean = keyboard_bits_in[2];
  assign increment_rundom_index = keyboard_bits_in[5];
  assign keyboard_bits_out = {end_message, 3'b000, empty_keyboard, keyboard_bits_in[2:0]};
  assign keyboard_clock = keyboard_bits_in[0];
  assign turn_off_on = keyboard_bits_in[1];
  assign update_random_number_for_bot = keyboard_bits_in[4];
  assign update_random_number_for_field = keyboard_bits_in[6];
endmodule

module random_field (
  input  cl,
  input  update_register,
  input  update_counter,
  output [7:0] cell_data
);

  wire [7:0] counter_1_q, register_1_q;
  wire [11:0] adder_1_out, counter_2_q, multiplier_1_out;

  Counter #(.max('h27)) counter_1 (.Q(counter_1_q), .clk(cl));  // open: load, D, count, carry, clr
  Register register_1 (.D(counter_1_q), .Q(register_1_q), .clk(update_register));  // open: en, clr
  // Probe on {4'b0000, register_1_q}
  // Probe on multiplier_1_out
  Multiplier #(.width(12)) multiplier_1 (
    .a({4'b0000, register_1_q}), .b(12'h64), .out(multiplier_1_out));  // open: cin, cout
  Counter #(.width(12), .max('h63)) counter_2 (
    .Q(counter_2_q), .clk(update_counter));  // open: load, D, count, carry, clr
  // Probe on counter_2_q
  Adder #(.width(12)) adder_1 (.a(multiplier_1_out), .b(counter_2_q), .out(adder_1_out));  // open: cin, cout
  // Probe on adder_1_out
  ROM #(.addrWidth(12)) rom_1 (.addr(adder_1_out), .data(cell_data));  // open: sel

  // Notes on the sheet:
  //   contents of rom_1 (hex, n*v repeats v):
  //   0 0 1b 0 0 1b 1b 14*0 1b 0 1b 0 0 0 1b 9*0 1b 0 0 0 4*1b 17*0 1b 4*0 1b 0 1b 0 0 1b 6*0 1b 0 0 1b
  //   6*0 1b 5*0 1b 8*0 1b 0 1b 1b 18*0 1b 0 0 1b 9*0 1b 1b 0 0 0 1b 0 1b 1b 0 1b 1b 8*0 1b 1b 0 0 0 1b 0
  //   1b 7*0 1b 9*0 1b 5*0 1b 1b 8*0 1b 6*0 1b 0 1b 11*0 1b 1b 1b 17*0 1b 9*0 1b 0 1b 0 1b 1b 13*0 1b 1b 0
  //   1b 0 0 0 1b 5*0 1b 0 0 0 1b 5*0 1b 0 0 0 1b 12*0 1b 1b 1b 5*0 1b 5*0 1b 1b 1b 17*0 1b 0 0 0 1b 1b
  //   12*0 4*1b 0 0 1b 9*0 1b 0 0 1b 13*0 1b 1b 0 1b 0 0 0 1b 6*0 1b 1b 12*0 1b 1b 1b 0 0 1b 19*0 1b 7*0
  //   1b 0 1b 13*0 1b 7*0 1b 8*0 1b 1b 4*0 1b 1b 1b 0 1b 1b 0 0 1b 6*0 1b 6*0 1b 4*0 1b 1b 0 1b 15*0 1b 0
  //   0 1b 9*0 1b 7*0 1b 6*0 1b 0 0 1b 0 0 1b 1b 1b 0 1b 0 0 1b 6*0 1b 0 0 1b 19*0 1b 0 1b 1b 0 0 1b 1b 1b
  //   18*0 1b 1b 1b 0 0 0 1b 9*0 1b 9*0 1b 7*0 1b 0 1b 0 0 0 1b 0 1b 7*0 1b 0 0 0 1b 1b 0 1b 5*0 1b 1b 0
  //   1b 12*0 1b 1b 0 0 0 1b 0 1b 18*0 4*1b 22*0 1b 0 1b 1b 12*0 1b 1b 1b 0 0 0 1b 1b 1b 8*0 1b 7*0 1b 9*0
  //   1b 0 1b 7*0 1b 0 0 0 4*1b 4*0 1b 9*0 1b 4*0 1b 6*0 1b 0 0 1b 0 0 1b 9*0 1b 11*0 1b 0 0 1b 1b 1b 6*0
  //   1b 5*0 1b 0 0 0 1b 0 1b 0 0 0 1b 0 1b 0 1b 5*0 1b 0 0 0 1b 0 1b 1b 14*0 1b 0 0 1b 9*0 1b 0 0 1b 1b 0
  //   1b 9*0 1b 9*0 1b 0 0 0 1b 8*0 1b 0 1b 1b 0 0 1b 1b 13*0 1b 5*0 1b 1b 1b 0 1b 13*0 1b 0 0 0 1b 0 0 1b
  //   1b 1b 4*0 1b 9*0 1b 0 1b 0 0 1b 4*0 1b 28*0 1b 1b 1b 0 0 1b 9*0 1b 6*0 1b 4*0 1b 1b 13*0 1b 1b 1b
  //   4*0 1b 6*0 1b 0 0 1b 0 0 1b 6*0 1b 7*0 1b 0 1b 0 0 0 1b 1b 15*0 1b 0 1b 1b 0 0 1b 0 1b 0 1b 21*0 1b
  //   0 0 0 1b 9*0 1b 0 1b 1b 1b 5*0 1b 5*0 1b 11*0 1b 1b 0 0 0 4*1b 5*0 1b 1b 12*0 1b 0 0 0 1b 1b 1b 0 1b
  //   22*0 1b 0 0 1b 0 0 1b 1b 0 0 1b 9*0 1b 0 0 1b 1b 1b 4*0 1b 0 0 1b 4*0 1b 4*0 1b 14*0 1b 1b 0 0 1b
  //   17*0 1b 0 0 0 1b 5*0 1b 5*0 1b 5*0 1b 0 0 0 1b 0 0 0 1b 0 1b 0 0 0 1b 0 1b 0 1b 0 1b 5*0 1b 7*0 1b 0
  //   1b 5*0 1b 0 0 0 1b 5*0 1b 0 0 1b 6*0 1b 0 0 1b 0 0 0 1b 1b 1b 11*0 1b 0 1b 9*0 1b 0 1b 0 0 1b 0 1b
  //   1b 0 1b 4*0 1b 4*0 1b 4*0 1b 13*0 1b 6*0 1b 14*0 1b 0 0 0 1b 1b 1b 0 0 0 1b 7*0 1b 0 1b 5*0 1b 0 1b
  //   0 1b 0 0 1b 4*0 1b 4*0 1b 7*0 1b 0 0 0 1b 0 1b 9*0 1b 13*0 1b 1b 1b 21*0 1b 0 0 0 1b 0 0 1b 6*0 1b
  //   4*0 1b 9*0 1b 0 0 1b 9*0 1b 0 1b 0 0 1b 1b 1b 12*0 1b 0 1b 0 0 0 1b 5*0 1b 0 0 0 1b 5*0 1b 0 0 0 1b
  //   4*0 1b 0 0 0 1b 0 0 1b 11*0 1b 1b 1b 0 0 1b 9*0 1b 0 0 0 1b 9*0 1b 16*0 1b 9*0 1b 0 1b 0 1b 0 0 1b 0
  //   0 1b 0 1b 0 1b 5*0 1b 0 1b 0 0 1b 5*0 1b 6*0 1b 0 0 1b 9*0 1b 0 0 1b 9*0 1b 12*0 1b 1b 1b 5*0 1b 6*0
  //   1b 1b 15*0 1b 0 0 0 4*1b 0 0 1b 0 1b 15*0 1b 0 0 0 1b 1b 1b 0 0 0 1b 11*0 1b 1b 1b 11*0 1b 7*0 1b 1b
  //   0 0 4*1b 22*0 1b 1b 0 1b 0 1b 0 0 1b 5*0 1b 0 0 1b 1b 12*0 1b 1b 0 1b 20*0 1b 1b 1b 0 0 0 1b 9*0 1b
  //   1b 8*0 1b 0 0 1b 0 1b 1b 1b 0 0 1b 15*0 1b 1b 8*0 1b 1b 1b 15*0 1b 0 0 1b 0 1b 0 0 1b 6*0 1b 4*0 1b
  //   0 1b 7*0 1b 0 1b 7*0 1b 13*0 4*1b 0 0 1b 9*0 1b 0 0 1b 6*0 4*1b 0 1b 1b 1b 15*0 1b 11*0 1b 1b 1b 0 0
  //   1b 1b 20*0 1b 1b 0 0 1b 1b 0 1b 16*0 1b 1b 17*0 1b 0 1b 1b 0 0 0 1b 12*0 1b 0 1b 0 0 1b 0 1b 0 0 1b
  //   0 1b 0 0 1b 6*0 1b 0 0 1b 11*0 4*1b 13*0 1b 6*0 1b 0 0 1b 19*0 1b 5*0 1b 0 1b 0 1b 0 0 0 1b 5*0 1b
  //   9*0 1b 16*0 1b 14*0 1b 1b 1b 0 1b 1b 1b 9*0 1b 0 1b 1b 0 0 0 1b 1b 1b 16*0 1b 0 0 1b 1b 0 0 0 1b 0
  //   1b 7*0 1b 5*0 1b 1b 0 0 1b 4*0 1b 4*0 1b 12*0 1b 0 0 1b 1b 1b 4*0 1b 0 1b 4*0 1b 0 0 1b 0 0 0 1b
  //   15*0 1b 6*0 1b 7*0 1b 6*0 1b 0 0 1b 6*0 1b 1b 0 1b 0 1b 0 1b 1b 4*0 1b 0 1b 9*0 1b 12*0 1b 1b 1b
  //   11*0 1b 1b 0 0 0 1b 8*0 1b 1b 1b 14*0 1b 0 0 0 1b 5*0 1b 9*0 1b 5*0 1b 1b 1b 0 1b 0 0 1b 20*0 1b 1b
  //   1b 0 0 0 1b 1b 12*0 1b 1b 0 1b 6*0 1b 0 0 1b 6*0 1b 0 0 0 1b 8*0 1b 13*0 4*1b 11*0 1b 1b 12*0 1b 1b
  //   1b 0 1b 1b 1b 17*0 1b 1b 0 1b 13*0 1b 0 1b 1b 0 1b 0 1b 7*0 1b 0 1b 9*0 1b 6*0 1b 4*0 1b 1b 0 1b
  //   12*0 1b 0 0 1b 1b 1b 12*0 4*1b 11*0 1b 0 0 0 1b 5*0 1b 9*0 1b 0 0 0 1b 1b 20*0 1b 1b 4*0 1b 9*0 1b 0
  //   1b 0 0 1b 0 0 1b 15*0 4*1b 0 0 1b 1b 1b 4*0 1b 1b 6*0 1b 6*0 1b 0 0 1b 0 0 1b 6*0 1b 6*0 1b 0 0 1b 0
  //   1b 0 0 1b 0 1b 4*0 1b 9*0 1b 8*0 1b 4*0 1b 1b 1b 4*0 1b 9*0 1b 9*0 1b 0 1b 0 1b 1b 1b 5*0 1b 6*0 1b
  //   0 0 1b 0 0 1b 0 0 0 1b 0 0 1b 21*0 1b 5*0 1b 1b 16*0 1b 1b 1b 5*0 1b 6*0 1b 0 0 1b 9*0 4*1b 0 1b 1b
  //   0 1b 22*0 1b 0 0 1b 0 0 0 1b 0 0 1b 0 0 1b 17*0 1b 0 1b 1b 1b 5*0 1b 7*0 1b 0 1b 0 0 0 1b 11*0 1b 0
  //   0 0 1b 5*0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
endmodule

module random_number (
  input  cl,
  input  update_random_number_for_field,
  output [7:0] cell_data
);

  wire [7:0] divider_1_rem, random_1_out;

  Random random_1 (.clk(cl), .out(random_1_out));  // open: next, clr
  Divider divider_1 (.a(random_1_out), .b(8'h64), .rem(divider_1_rem));  // open: out, upper
  Register register_1 (.D(divider_1_rem), .Q(cell_data), .clk(update_random_number_for_field));  // open: en, clr
endmodule
